# Fritzing sketch ESP-LOLIN32-Tonuino V1 (saved by Fritzing 0.9.3b)
circuit board: 8.46667cm x 5.64444cm
breadboards: 1

parts:
  U1 = lolin
  SD-MMC = female pin header, 6 pins [form="♀ (female)"]
  Neopixel = female pin header, 3 pins [form="♀ (female)"]
  RFID_PN5180 = female pin header, 10 pins [form="♀ (female)"]
  MAX98357a = female pin header, 7 pins [form="♀ (female)"]
  JUMPER = female pin header, 3 pins [form="♀ (female)"]
  Rotery_Encoder = female pin header, 5 pins [form="♀ (female)"]
  Button = female pin header, 4 pins [form="♀ (female)"]
  BAT = female pin header, 2 pins [form="♀ (female)"]
  BAT1 = female pin header, 2 pins [form="♀ (female)"]
  ButtonGND = female pin header, 4 pins [form="♀ (female)"]
  R1 = Resistor [tolerance=±5% resistance=10k package=THT]
  R2 = Resistor [tolerance=±5% resistance=100k package=THT]
  R3 = Resistor [tolerance=±1% resistance=100k package=THT]
  R4 = Resistor [tolerance=±1% resistance=100k package=THT]
  C1 = Electrolytic Capacitor [capacitance=10µF package="100 mil [THT, electrolytic]"]
  SD-MMC_2 = female pin header, 6 pins [form="♀ (female)"]
  Q1 = Basic FET P-Channel [part_number=IRL3103 package="TO220 [THT]"]
  R5 = Resistor [tolerance=±5% resistance=100k package=THT]
  R6 = Resistor [tolerance=±5% resistance=1k package=THT]
  R7 = Resistor [tolerance=±5% resistance=10k package=THT]
  Q2 = Basic FET N-Channel [part_number=NDP6020P package="TO220 [THT]"]
  J1 = shrouded pin header, 6 pins [form="♂ (shrouded male)" part_number="to headphone"]
  SERIAL = female pin header, 3 pins [form="♀ (female)"]
  Bauteil2 = RFID-RC522-v2
  JP1 = Header 2 [package=jst-2-pth-ns]

nets:
  3.3V: U1.connector0, U1.connector25, U1.connector34, JUMPER.pin3, Rotery_Encoder.pin2, R5.Pin_0, Q2.source
  EN: U1.connector1, Button.pin1
  BUT_PREV: U1.connector2, Button.pin3, R1.Pin_0
  RFID_IRQ: U1.connector3, RFID_PN5180.pin9
  ROTENC_BUT: U1.connector4, Rotery_Encoder.pin3
  VBAT: U1.connector5, R3.Pin_0, R4.Pin_0
  ROTENC_CLK: U1.connector6, Rotery_Encoder.pin4
  ROTENC_DT: U1.connector7, Rotery_Encoder.pin5
  I2S_DOUT: U1.connector8, MAX98357a.pin5, J1.pin1
  I2S_LRC: U1.connector9, MAX98357a.pin7, J1.pin5
  I2S_BCLK: U1.connector10, MAX98357a.pin6, J1.pin3
  MMC_SCK: U1.connector11, SD-MMC.pin3, SD-MMC_2.pin3
  NEOPIXEL: U1.connector12, Neopixel.pin2
  HEADPHONE: U1.connector13, MAX98357a.pin3, J1.pin6
  GND: U1.connector15, U1.connector17, U1.connector20, U1.connector30, U1.connector31, U1.connector37, SD-MMC.pin1, Neopixel.pin3, RFID_PN5180.pin10, MAX98357a.pin2, Rotery_Encoder.pin1, ButtonGND.pin1, ButtonGND.pin2, ButtonGND.pin3, ButtonGND.pin4, SD-MMC_2.pin1, Q1.source, R7.Pin_1, J1.pin4, SERIAL.pin1, Bauteil2.GND
  MMC_MOSI: U1.connector18, SD-MMC.pin4, SD-MMC_2.pin4
  MMC_MISO: U1.connector19, SD-MMC.pin2, SD-MMC_2.pin2
  BUT_NEXT: U1.connector22, Button.pin2
  BUT_PPLAY/RFID_BUSY: U1.connector23, U1.connector26, RFID_PN5180.pin8, Button.pin4
  N1: U1.connector24, R6.Pin_0
  RFID_SCK: U1.connector27, RFID_PN5180.pin7, Bauteil2.SCK
  RFID_MOSI: U1.connector28, RFID_PN5180.pin5, Bauteil2.MOSI
  RFID_MISO: U1.connector29, RFID_PN5180.pin6, Bauteil2.MISO
  RFID_CS: U1.connector32, RFID_PN5180.pin4, Bauteil2.SDA
  RFID_RST: U1.connector33, RFID_PN5180.pin3
  N2: U1.connector35, SERIAL.pin3
  N3: U1.connector36, SERIAL.pin2
  SW_POWER3.3V: SD-MMC.pin6, Neopixel.pin1, MAX98357a.pin1, JUMPER.pin1, R1.Pin_1, R2.Pin_1, SD-MMC_2.pin6, Q2.drain, J1.pin2, Bauteil2.RST, Bauteil2.3.3V
  N4: RFID_PN5180.pin1, RFID_PN5180.pin2, JUMPER.pin2
  N5: MAX98357a.pin4, R2.Pin_0
  N6: BAT.pin1, BAT1.pin1, R3.Pin_1, C1.+, JP1.2
  N7: BAT.pin2, BAT1.pin2, R4.Pin_1, C1.-, JP1.1
  N8: Q1.gate, R6.Pin_1, R7.Pin_0
  N9: Q1.drain, R5.Pin_1, Q2.gate

notes:
  IRL3103
  NDP6020P
  10k
  100k
  1k
  3.3V SW_Power
  +  -
  GND
  MISO
  MOSI
  SCK
  Vcc
  NC
  RST
  CS
  BUSY
  IRQ
  G T R
  Headp
  DOUT
  BCLK
  LRC
  BUT
  CLK
  DT
  Neo
  Reset
  Next
  Prev
  Play
  Version 1.0
  ESPuino-PCB
  + -
  Sascha Ludwig
  LOLIN32

custom parts:
  RFID-RC522-v2: A simple China made RFID-RC522 Reader; do check the pin labels, as this is a MFRC522 based clone.
